// Logisim project 4_bit_carry_look_ahead_adder.circ as structural Verilog: 1 circuit, main circuit main
module main (
  input  C0,
  input  [3:0] X,
  input  [3:0] Y
);

  wire and_1_out, and_2_out, and_3_out, and_4_out, and_5_out, and_6_out, and_7_out, and_8_out, and_9_out,
       and_10_out, and_11_out, and_12_out, and_13_out, and_14_out, or_1_out, or_2_out, or_3_out, xor_1_out,
       xor_2_out, xor_3_out, xor_4_out;
  wire [0:0] or_4_out;
  wire [3:0] xor_5_out;

  xor xor_1 (xor_1_out, X[0], Y[0]);
  and and_1 (and_1_out, X[0], Y[0]);
  xor xor_2 (xor_2_out, X[1], Y[1]);
  and and_2 (and_2_out, X[1], Y[1]);
  xor xor_3 (xor_3_out, X[2], Y[2]);
  and and_3 (and_3_out, X[2], Y[2]);
  xor xor_4 (xor_4_out, X[3], Y[3]);
  and and_4 (and_4_out, X[3], Y[3]);
  and and_5 (and_5_out, C0, xor_1_out);
  and and_6 (and_6_out, C0, xor_1_out, xor_2_out);
  and and_7 (and_7_out, xor_2_out, and_1_out);
  and and_8 (and_8_out, C0, xor_1_out, xor_2_out, xor_3_out);
  and and_9 (and_9_out, and_1_out, xor_2_out, xor_3_out);
  and and_10 (and_10_out, and_2_out, xor_3_out);
  and and_11 (and_11_out, xor_4_out, xor_3_out, xor_2_out, xor_1_out, C0);
  and and_12 (and_12_out, and_1_out, xor_2_out, xor_3_out, xor_4_out);
  and and_13 (and_13_out, and_2_out, xor_3_out, xor_4_out);
  and and_14 (and_14_out, and_3_out, xor_4_out);
  or or_1 (or_1_out, and_5_out, and_1_out);
  or or_2 (or_2_out, and_6_out, and_7_out, and_2_out);
  or or_3 (or_3_out, and_8_out, and_9_out, and_10_out, and_3_out);
  or or_4 (or_4_out[0], and_11_out, and_12_out, and_13_out, and_14_out, and_4_out);
  xor xor_5 (xor_5_out[0], xor_1_out, C0);
  xor xor_6 (xor_5_out[1], xor_2_out, or_1_out);
  xor xor_7 (xor_5_out[2], or_2_out, xor_3_out);
  xor xor_8 (xor_5_out[3], or_3_out, xor_4_out);
  Hex_Digit_Display hex_digit_display_1 (.value({3'b000, or_4_out[0]}));  // open: dp
  Hex_Digit_Display hex_digit_display_2 (.value(xor_5_out));  // open: dp
endmodule
