// Logisim project 4_bit_comparator.circ as structural Verilog: 1 circuit, main circuit main
module main (
  input  [3:0] A,
  input  [3:0] B,
  output A_greater_than_B,
  output A_equal_to_B,
  output A_less_than_B
);

  wire and_1_out, and_2_out, and_3_out, and_4_out, and_5_out, and_6_out, and_7_out, and_8_out, and_9_out,
       and_10_out, and_11_out, and_12_out, and_13_out, and_14_out, and_15_out, and_16_out, nor_1_out,
       nor_2_out, nor_3_out, nor_4_out, not_1_out, not_2_out, not_3_out, not_4_out, not_5_out, not_6_out,
       not_7_out, not_8_out;

  not not_1 (not_1_out, B[3]);
  not not_2 (not_2_out, A[3]);
  not not_3 (not_3_out, B[2]);
  not not_4 (not_4_out, A[2]);
  and and_1 (and_1_out, A[3], not_1_out);
  and and_2 (and_2_out, not_2_out, B[3]);
  and and_3 (and_3_out, A[2], not_3_out);
  and and_4 (and_4_out, not_4_out, B[2]);
  not not_5 (not_5_out, B[1]);
  not not_6 (not_6_out, A[1]);
  not not_7 (not_7_out, B[0]);
  not not_8 (not_8_out, A[0]);
  nor nor_1 (nor_1_out, and_1_out, and_2_out);
  nor nor_2 (nor_2_out, and_3_out, and_4_out);
  and and_5 (and_5_out, A[1], not_5_out);
  and and_6 (and_6_out, not_6_out, B[1]);
  and and_7 (and_7_out, A[0], not_7_out);
  and and_8 (and_8_out, not_8_out, B[0]);
  and and_9 (and_9_out, nor_1_out, and_3_out);
  and and_10 (and_10_out, nor_1_out, nor_2_out);
  nor nor_3 (nor_3_out, and_5_out, and_6_out);
  and and_11 (and_11_out, and_4_out, nor_1_out);
  and and_12 (and_12_out, and_10_out, and_5_out);
  and and_13 (and_13_out, and_6_out, and_10_out);
  and and_14 (and_14_out, and_10_out, nor_3_out);
  nor nor_4 (nor_4_out, and_7_out, and_8_out);
  and and_15 (and_15_out, and_14_out, and_7_out);
  and and_16 (and_16_out, and_14_out, and_8_out);
  or or_1 (A_greater_than_B, and_1_out, and_9_out, and_12_out, and_15_out);
  and and_17 (A_equal_to_B, and_14_out, nor_4_out);
  or or_2 (A_less_than_B, and_16_out, and_13_out, and_11_out, and_2_out);
endmodule
