// Logisim project universal_shift_registers.circ as structural Verilog: 1 circuit, main circuit main
module main (
  input  I4,
  input  I3,
  input  I2,
  input  I1,
  input  Dl,
  input  Dr,
  input  S1,
  input  in_8,
  input  S2,
  output O4,
  output O3,
  output O2,
  output O1
);

  wire clk_out, multiplexer_1_out, multiplexer_2_out, multiplexer_3_out, multiplexer_4_out;

  Clock clk (.out(clk_out));
  Multiplexer #(.select(2)) multiplexer_1 (
    .in0(O4), .in1(Dr), .in2(O3), .in3(I4), .out(multiplexer_1_out), .sel({S2, S1}));
  D_Flip_Flop d_ff_1 (.D(multiplexer_1_out), .clk(clk_out), .Q(O4), .preset(in_8), .reset(in_8));  // open: Qn
  D_Flip_Flop d_ff_2 (.D(multiplexer_2_out), .clk(clk_out), .Q(O3), .preset(in_8), .reset(in_8));  // open: Qn
  Multiplexer #(.select(2)) multiplexer_2 (
    .in0(O3), .in1(O4), .in2(O2), .in3(I3), .out(multiplexer_2_out), .sel({S2, S1}));
  Multiplexer #(.select(2)) multiplexer_3 (
    .in0(O2), .in1(O3), .in2(O1), .in3(I2), .out(multiplexer_3_out), .sel({S2, S1}));
  D_Flip_Flop d_ff_3 (.D(multiplexer_3_out), .clk(clk_out), .Q(O2), .preset(in_8), .reset(in_8));  // open: Qn
  Multiplexer #(.select(2)) multiplexer_4 (
    .in0(O1), .in1(O2), .in2(Dl), .in3(I1), .out(multiplexer_4_out), .sel({S2, S1}));
  D_Flip_Flop d_ff_4 (.D(multiplexer_4_out), .clk(clk_out), .Q(O1), .preset(in_8), .reset(in_8));  // open: Qn
endmodule
